# Fritzing sketch rx (saved by Fritzing 0.9.3b)

parts:
  Part1 = Arduino Uno (Rev3) - ICSP
  U1 = RF-LINK_RX [package=rf-link_rx]

nets:
  N1: Part1.D11_PWM/MOSI, U1.Data
  5V: Part1.5V, U1.VCC
  GND: Part1.GND, U1.GND

custom parts:
  RF-LINK_RX: RF Link receivers- WRL-8947, 8948, 8949, 8950
