# Fritzing sketch tx (saved by Fritzing 0.9.3b)
breadboards: 1

parts:
  Part1 = Arduino Nano (Rev3.0) (ICSP)
  U3 = FS1000A - 433Mhz RF Transmitter [package=THT]
  R1 = Rotary Potentiometer (Small) [maximum_resistance=100kΩ package=THT]

nets:
  GND: Part1.GND, U3.GND, R1.leg1
  N1: Part1.D12/MISO, U3.DATA
  5V: Part1.5V, U3.VCC, R1.leg2
  N2: Part1.A0, R1.wiper

custom parts:
  FS1000A - 433Mhz RF Transmitter: This is 433Mhz RF transmitter with receiver kit for Arduino ARM MCU wireless Application environment: Remote control switch, receiver module, motorcycles, automobile anti-theft products, home security products, electric doors, shutter doors, windows, remote control socket, remote control LED, remote audio remote control electric doors, garage door remote control, remote control retractable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
